// Logisim project Trabalho2Circuito.circ as structural Verilog
module display (
  input  Chutar,
  input  Proximo,
  input  B3,
  input  B2,
  input  B1,
  input  B0,
  input  B3_2,
  input  B2_2,
  input  B1_2,
  input  B0_2,
  output Errou,
  output Acertou,
  output Menor,
  output Igual,
  output Maior
);

  wire and_1_out, and_2_out, and_3_out, and_4_out, button_1_out, d_ff_1_q, d_ff_2_q, d_ff_3_q, d_ff_4_q,
       decodificador_1_a_2, decodificador_1_b_2, decodificador_1_c_2, decodificador_1_d_2, decodificador_1_e,
       decodificador_1_f, decodificador_1_g, decodificador_2_a_2, decodificador_2_b_2, decodificador_2_c_2,
       decodificador_2_d_2, decodificador_2_e, decodificador_2_f, decodificador_2_g, not_1_out, not_2_out,
       not_3_out, or_1_out, or_2_out, registrador_1_s1, registrador_1_s2, registrador_1_s3, registrador_1_s4,
       registrador_2_s1, registrador_2_s2, registrador_2_s3, registrador_2_s4, valoresplano_1_led,
       valoresplano_2_led;
  wire [3:0] multiplexer_1_out, valoresplano_1_valores_de_saida, valoresplano_2_valores_de_saida;

  LED led_1 (.in(valoresplano_1_led));
  Hex_Digit_Display hex_digit_display_1 (.value(valoresplano_1_valores_de_saida));  // open: dp
  ValoresPlano valoresplano_1 (
    .valores_de_entrada({B3, B2, B1, B0}), .valores_de_saida(valoresplano_1_valores_de_saida),
    .led(valoresplano_1_led));
  LED led_2 (.in(or_1_out));
  or or_1 (or_1_out, and_1_out, and_2_out);
  and and_1 (and_1_out, ~Proximo, d_ff_1_q);  // AND_Gate
  Comparador comparador_1 (
    .in_1(button_1_out), .valorX(multiplexer_1_out), .valorY(multiplexer_1_out), .Errou(Errou),
    .Acertou(Acertou), .Menor(Menor), .Igual(Igual), .Maior(Maior));  // open: Random2, Random1
  Button button_1 (.out(button_1_out));
  _7_Segment_Display u_7_segment_display_1 (
    .g(decodificador_1_g), .f(decodificador_1_f), .a(decodificador_1_a_2), .b(decodificador_1_b_2),
    .e(decodificador_1_e), .d(decodificador_1_d_2), .c(decodificador_1_c_2));  // open: dp
  decodificador decodificador_1 (
    .a(registrador_1_s1), .b(registrador_1_s2), .c(registrador_1_s3), .d(registrador_1_s4),
    .a_2(decodificador_1_a_2), .b_2(decodificador_1_b_2), .c_2(decodificador_1_c_2),
    .d_2(decodificador_1_d_2), .e(decodificador_1_e), .f(decodificador_1_f), .g(decodificador_1_g));
  Registrador registrador_1 (
    .S1(registrador_1_s1), .S2(registrador_1_s2), .S3(registrador_1_s3), .S4(registrador_1_s4),
    .botao(Chutar), .B1(multiplexer_1_out[3]), .B2(multiplexer_1_out[2]), .B3(multiplexer_1_out[1]),
    .B4(multiplexer_1_out[0]));
  and and_2 (and_2_out, Proximo, d_ff_3_q);
  Multiplexer #(.width(4)) multiplexer_1 (
    .in0(valoresplano_1_valores_de_saida), .in1(valoresplano_2_valores_de_saida), .out(multiplexer_1_out),
    .sel(Proximo));  // open: en
  D_Flip_Flop d_ff_1 (.clk(Chutar), .D(valoresplano_1_led), .Q(d_ff_1_q));  // open: Qn, preset, en, reset
  not not_1 (not_1_out, Chutar);
  D_Flip_Flop d_ff_2 (.clk(not_2_out), .D(valoresplano_1_led), .Q(d_ff_2_q));  // open: Qn, preset, en, reset
  not not_2 (not_2_out, Chutar);
  LED led_3 (.in(or_2_out));
  decodificador decodificador_2 (
    .a(registrador_2_s1), .b(registrador_2_s2), .c(registrador_2_s3), .d(registrador_2_s4),
    .a_2(decodificador_2_a_2), .b_2(decodificador_2_b_2), .c_2(decodificador_2_c_2),
    .d_2(decodificador_2_d_2), .e(decodificador_2_e), .f(decodificador_2_f), .g(decodificador_2_g));
  D_Flip_Flop d_ff_3 (.clk(Chutar), .D(valoresplano_2_led), .Q(d_ff_3_q));  // open: Qn, preset, en, reset
  _7_Segment_Display u_7_segment_display_2 (
    .g(decodificador_2_g), .f(decodificador_2_f), .a(decodificador_2_a_2), .b(decodificador_2_b_2),
    .e(decodificador_2_e), .d(decodificador_2_d_2), .c(decodificador_2_c_2));  // open: dp
  Registrador registrador_2 (
    .S1(registrador_2_s1), .S2(registrador_2_s2), .S3(registrador_2_s3), .S4(registrador_2_s4),
    .botao(not_1_out), .B1(multiplexer_1_out[3]), .B2(multiplexer_1_out[2]), .B3(multiplexer_1_out[1]),
    .B4(multiplexer_1_out[0]));
  not not_3 (not_3_out, Chutar);
  D_Flip_Flop d_ff_4 (.clk(not_3_out), .D(valoresplano_2_led), .Q(d_ff_4_q));  // open: Qn, preset, en, reset
  or or_2 (or_2_out, and_3_out, and_4_out);
  and and_3 (and_3_out, ~Proximo, d_ff_2_q);  // AND_Gate
  and and_4 (and_4_out, Proximo, d_ff_4_q);
  ValoresPlano valoresplano_2 (
    .valores_de_entrada({B3_2, B2_2, B1_2, B0_2}), .valores_de_saida(valoresplano_2_valores_de_saida),
    .led(valoresplano_2_led));
  LED led_4 (.in(valoresplano_2_led));
  Hex_Digit_Display hex_digit_display_2 (.value(valoresplano_2_valores_de_saida));  // open: dp
endmodule

module decodificador (
  input  a,
  input  b,
  input  c,
  input  d,
  output a_2,
  output b_2,
  output c_2,
  output d_2,
  output e,
  output f,
  output g
);

  wire and_1_out, and_2_out, and_3_out, and_4_out, and_5_out, and_6_out, and_7_out, and_8_out, and_9_out,
       and_10_out, and_11_out, and_12_out, and_13_out, and_14_out, and_15_out, and_16_out, and_17_out,
       and_18_out, and_19_out, and_20_out, and_21_out, and_22_out, and_23_out, and_24_out, and_25_out,
       and_26_out, and_27_out, and_28_out, and_29_out, and_30_out, and_31_out, and_32_out, and_33_out,
       and_34_out;

  and and_1 (and_1_out, ~b, ~d);  // AND_Gate
  and and_2 (and_2_out, ~a, c);  // AND_Gate
  and and_3 (and_3_out, ~a, b, d);  // AND_Gate
  and and_4 (and_4_out, b, c);
  and and_5 (and_5_out, a, ~b, ~c);  // AND_Gate
  and and_6 (and_6_out, a, ~d);  // AND_Gate
  and and_7 (and_7_out, ~a, ~c, ~d);  // AND_Gate
  and and_8 (and_8_out, ~b, ~d);  // AND_Gate
  and and_9 (and_9_out, ~a, c, d);  // AND_Gate
  and and_10 (and_10_out, a, ~c, d);  // AND_Gate
  and and_11 (and_11_out, ~a, ~c, ~d);  // AND_Gate
  and and_12 (and_12_out, ~a, c, d);  // AND_Gate
  and and_13 (and_13_out, ~a, b);  // AND_Gate
  and and_14 (and_14_out, a, ~b);  // AND_Gate
  and and_15 (and_15_out, a, ~c, d);  // AND_Gate
  and and_16 (and_16_out, ~a, ~b, ~d);  // AND_Gate
  and and_17 (and_17_out, ~b, c, d);  // AND_Gate
  and and_18 (and_18_out, b, ~c, d);  // AND_Gate
  and and_19 (and_19_out, b, c, ~d);  // AND_Gate
  and and_20 (and_20_out, a, ~c);  // AND_Gate
  and and_21 (and_21_out, ~a, ~b, ~c);  // AND_Gate
  and and_22 (and_22_out, ~b, ~d);  // AND_Gate
  and and_23 (and_23_out, c, ~d);  // AND_Gate
  and and_24 (and_24_out, a, c);
  and and_25 (and_25_out, a, b);
  and and_26 (and_26_out, ~a, ~c);  // AND_Gate
  and and_27 (and_27_out, ~c, ~d);  // AND_Gate
  and and_28 (and_28_out, b, c);
  and and_29 (and_29_out, a, ~b);  // AND_Gate
  and and_30 (and_30_out, ~b, c);  // AND_Gate
  and and_31 (and_31_out, c, ~d);  // AND_Gate
  and and_32 (and_32_out, ~a, b, ~c);  // AND_Gate
  and and_33 (and_33_out, a, ~b);  // AND_Gate
  and and_34 (and_34_out, a, d);
  or or_1 (a_2, and_1_out, and_2_out, and_3_out, and_4_out, and_5_out, and_6_out);
  or or_2 (b_2, and_7_out, and_8_out, and_9_out, and_10_out);
  or or_3 (c_2, and_11_out, and_12_out, and_13_out, and_14_out, and_15_out);
  or or_4 (d_2, and_16_out, and_17_out, and_18_out, and_19_out, and_20_out);
  or or_5 (e, and_21_out, and_22_out, and_23_out, and_24_out, and_25_out);
  or or_6 (f, and_26_out, and_27_out, and_28_out, and_29_out);
  or or_7 (g, and_30_out, and_31_out, and_32_out, and_33_out, and_34_out);
endmodule

module reserva (
  input  A0,
  input  A1,
  input  A2,
  input  A3
);

  wire decodificador_1_a_2, decodificador_1_b_2, decodificador_1_c_2, decodificador_1_d_2, decodificador_1_e,
       decodificador_1_f, decodificador_1_g;

  _7_Segment_Display u_7_segment_display_1 (
    .g(decodificador_1_g), .f(decodificador_1_f), .a(decodificador_1_a_2), .b(decodificador_1_b_2),
    .e(decodificador_1_e), .d(decodificador_1_d_2), .c(decodificador_1_c_2));  // open: dp
  decodificador decodificador_1 (
    .a(A0), .b(A1), .c(A2), .d(A3), .a_2(decodificador_1_a_2), .b_2(decodificador_1_b_2),
    .c_2(decodificador_1_c_2), .d_2(decodificador_1_d_2), .e(decodificador_1_e), .f(decodificador_1_f),
    .g(decodificador_1_g));
endmodule

module Registrador (
  input  botao,
  input  B1,
  input  B2,
  input  B3,
  input  B4,
  output S1,
  output S2,
  output S3,
  output S4
);

  D_Flip_Flop d_ff_1 (.clk(botao), .D(B1), .Q(S1));  // open: Qn, preset, en, reset
  D_Flip_Flop d_ff_2 (.clk(botao), .D(B2), .Q(S2));  // open: Qn, preset, en, reset
  D_Flip_Flop d_ff_3 (.clk(botao), .D(B3), .Q(S3));  // open: Qn, preset, en, reset
  D_Flip_Flop d_ff_4 (.clk(botao), .D(B4), .Q(S4));  // open: Qn, preset, en, reset
endmodule

module ValoresPlano (
  input  [3:0] valores_de_entrada,
  output [3:0] valores_de_saida,
  output led
);

  wire [3:0] adder_1_out, not_4_out;

  not not_1 (not_4_out[3], valores_de_entrada[3]);
  not not_2 (not_4_out[2], valores_de_entrada[2]);
  not not_3 (not_4_out[1], valores_de_entrada[1]);
  not not_4 (not_4_out[0], valores_de_entrada[0]);
  Multiplexer #(.width(4)) multiplexer_1 (
    .in0(valores_de_entrada), .in1(adder_1_out), .out(valores_de_saida), .sel(valores_de_entrada[3]));  // open: en
  Adder #(.width(4)) adder_1 (.a(not_4_out), .b(4'b0001), .out(adder_1_out));  // open: cin, cout

  assign led = valores_de_entrada[3];
endmodule

module Comparador (
  input  in_1,
  input  [3:0] valorX,
  input  [3:0] valorY,
  output Errou,
  output Acertou,
  output [3:0] Random1,
  output Menor,
  output [3:0] Random2,
  output Igual,
  output Maior
);

  wire comparator_1_eq;
  wire [3:0] adder_1_out, adder_2_out;

  Random #(.width(4)) random_1 (.clk(in_1), .out(Random1));  // open: next, clr
  Random #(.width(4)) random_2 (.clk(in_1), .out(Random2));  // open: next, clr
  Adder #(.width(4)) adder_1 (.a(valorX), .b(valorY), .out(adder_1_out));  // open: cin, cout
  Adder #(.width(4)) adder_2 (.a(Random1), .b(Random2), .out(adder_2_out));  // open: cin, cout
  Comparator #(.width(4)) comparator_1 (.a(Random1), .b(valorX), .eq(comparator_1_eq));  // open: gt, lt
  Comparator #(.width(4)) comparator_2 (.a(adder_2_out), .b(adder_1_out), .gt(Menor), .eq(Igual), .lt(Maior));
  and and_1 (Acertou, comparator_1_eq, Igual);
  not not_1 (Errou, Acertou);
endmodule
