// Logisim project guess-the-number.circ as structural Verilog: 14 circuits, main circuit main
module main (
  input  A3,
  input  A2,
  input  A1,
  input  A0,
  input  B3,
  input  B2,
  input  B1,
  input  B0
);

  wire A_jogando, A_venceu, acertou, ADEAD, and_1_out, and_2_out, and_3_out, and_4_out, and_5_out, B_jogando,
       B_venceu, BDEAD, c, Chutando_X, Chutando_Y, chutar, clock_1_out, configurar, dma_t, dmb_t, dsa_t,
       dsb_t, Empate, Fim_de_jogo, igual, maior, menor, multiplexer_1_out, placar_1_fim_de_jogo, proximo,
       reset, rodando, SA, SB, start, SX, SY, uma_t, umb_t, usa_t, usb_t;
  wire [3:0] core_1_x_chutado_no_momento, core_1_y_chutado_no_momento, DMA, DMB, DSA, DSB, GA, GB, PA, PB,
       UMA, UMB, USA, USB, XH, YH;

  Button button_1 (.out(dma_t));
  Hex_Digit_Display hex_digit_display_1 (.value(DMA));  // open: dp
  Hex_Digit_Display hex_digit_display_2 (.value(PA));  // open: dp
  Button button_2 (.out(uma_t));
  Hex_Digit_Display hex_digit_display_3 (.value(UMA));  // open: dp
  LED led_1 (.in(SA));
  Hex_Digit_Display hex_digit_display_4 (.value(GA));  // open: dp
  LED led_2 (.in(A_jogando));
  Button button_3 (.out(usa_t));
  Button button_4 (.out(dsa_t));
  Hex_Digit_Display hex_digit_display_5 (.value(USA));  // open: dp
  Hex_Digit_Display hex_digit_display_6 (.value(DSA));  // open: dp
  LED led_3 (.in(A_venceu));
  LED led_4 (.in(rodando));
  Button button_5 (.out(start));
  LED led_5 (.in(maior));
  LED led_6 (.in(SX));
  Hex_Digit_Display hex_digit_display_7 (.value(XH));  // open: dp
  LED led_7 (.in(Chutando_X));
  LED led_8 (.in(Fim_de_jogo));
  LED led_9 (.in(Empate));
  LED led_10 (.in(c));
  Button button_6 (.out(configurar));
  LED led_11 (.in(acertou));
  LED led_12 (.in(igual));
  Button button_7 (.out(proximo));
  Button button_8 (.out(chutar));
  LED led_13 (.in(SY));
  LED led_14 (.in(B_venceu));
  Button button_9 (.out(reset));
  LED led_15 (.in(menor));
  Hex_Digit_Display hex_digit_display_8 (.value(YH));  // open: dp
  LED led_16 (.in(Chutando_Y));
  Button button_10 (.out(dmb_t));
  Hex_Digit_Display hex_digit_display_9 (.value(DMB));  // open: dp
  Hex_Digit_Display hex_digit_display_10 (.value(PB));  // open: dp
  Button button_11 (.out(umb_t));
  Hex_Digit_Display hex_digit_display_11 (.value(UMB));  // open: dp
  LED led_17 (.in(SB));
  Hex_Digit_Display hex_digit_display_12 (.value(GB));  // open: dp
  LED led_18 (.in(B_jogando));
  Button button_12 (.out(usb_t));
  Button button_13 (.out(dsb_t));
  Hex_Digit_Display hex_digit_display_13 (.value(DSB));  // open: dp
  Hex_Digit_Display hex_digit_display_14 (.value(USB));  // open: dp
  and and_1 (and_1_out, acertou, A_jogando);
  and and_2 (and_2_out, acertou, B_jogando);
  ValoresPlano valoresplano_1 (.Valores_de_entrada({A3, A2, A1, A0}), .Valores_de_saida(GA), .Sinal_negativo(SA));
  ValoresPlano valoresplano_2 (.Valores_de_entrada({B3, B2, B1, B0}), .Valores_de_saida(GB), .Sinal_negativo(SB));
  Placar placar_1 (
    .A_pontuou(and_1_out), .B_pontuou(and_2_out), .Reset(reset), .Placar_A(PA), .Placar_B(PB),
    .A_venceu(A_venceu), .B_venceu(B_venceu), .Empate(Empate), .Fim_de_jogo(placar_1_fim_de_jogo));
  ValoresPlano valoresplano_3 (
    .Valores_de_entrada(core_1_x_chutado_no_momento), .Valores_de_saida(XH), .Sinal_negativo(SX));
  and and_3 (and_3_out, ADEAD, BDEAD);
  Core core_1 (
    .Chute_do_jogador_A({A3, A2, A1, A0}), .A_DEAD(ADEAD), .Chute_do_jogador_B({B3, B2, B1, B0}),
    .B_DEAD(BDEAD), .Chutar(chutar), .\Próximo (proximo), .Reset(reset),
    .X_chutado_no_momento(core_1_x_chutado_no_momento), .Y_chutado_no_momento(core_1_y_chutado_no_momento),
    .Maior(maior), .Igual(igual), .Menor(menor), .Acertou(acertou), .Aguardando_chute_Y(Chutando_Y),
    .Aguardando_chute_X(Chutando_X), .Turno__0___A__1___B(B_jogando), .\Gerar_aleatório (start));  // open: Exibindo_resultado_do_chute
  not not_1 (A_jogando, B_jogando);
  ValoresPlano valoresplano_4 (
    .Valores_de_entrada(core_1_y_chutado_no_momento), .Valores_de_saida(YH), .Sinal_negativo(SY));
  or or_1 (Fim_de_jogo, and_3_out, placar_1_fim_de_jogo);
  and and_4 (and_4_out, B_jogando, rodando);
  T_Flip_Flop t_ff_1 (.clk(configurar), .T(configurar), .Q(c));  // open: Qn, preset, reset, en
  Multiplexer multiplexer_1 (.in0(1'b0), .in1(clock_1_out), .out(multiplexer_1_out), .sel(rodando));  // open: en
  \Cronômetro  \cronômetro_1  (
    .End(ADEAD), .Dezena_de_minuto(DMA), .Unidade_de_minuto(UMA), .Dezena_de_segundo(DSA),
    .Unidade_de_segundo(USA), .Clock(multiplexer_1_out), .Pause(and_4_out), .Config(c), .Clear(reset),
    .Altera_dezena_de_minuto(dma_t), .Altera_unidade_de_minuto(uma_t), .Altera_dezena_de_segundo(dsa_t),
    .Altera_unidade_de_segundo(usa_t));
  \Cronômetro  \cronômetro_2  (
    .End(BDEAD), .Dezena_de_minuto(DMB), .Unidade_de_minuto(UMB), .Dezena_de_segundo(DSB),
    .Unidade_de_segundo(USB), .Clock(multiplexer_1_out), .Pause(and_5_out), .Config(c), .Clear(reset),
    .Altera_dezena_de_minuto(dmb_t), .Altera_unidade_de_minuto(umb_t), .Altera_dezena_de_segundo(dsb_t),
    .Altera_unidade_de_segundo(usb_t));
  Clock clock_1 (.out(clock_1_out));
  T_Flip_Flop t_ff_2 (.clk(start), .T(start), .Q(rodando));  // open: Qn, preset, reset, en
  and and_5 (and_5_out, A_jogando, rodando);
endmodule

module Core (
  input  Reset,
  input  [3:0] Chute_do_jogador_A,
  input  A_DEAD,
  input  Chutar,
  input  \Próximo ,
  input  [3:0] Chute_do_jogador_B,
  input  B_DEAD,
  input  \Gerar_aleatório ,
  output Aguardando_chute_Y,
  output Aguardando_chute_X,
  output Exibindo_resultado_do_chute,
  output Turno__0___A__1___B,
  output [3:0] X_chutado_no_momento,
  output [3:0] Y_chutado_no_momento,
  output Maior,
  output Menor,
  output Acertou,
  output Igual
);

  wire and_1_out, and_2_out, comparador_de_palpites_1_acertou, comparador_de_palpites_1_igual,
       comparador_de_palpites_1_maior, comparador_de_palpites_1_menor, Coordenada__0___X__1___Y_q,
       Coordenada__0___X__1___Y_qn, not_1_out, not_2_out;
  wire [3:0] multiplexer_1_out, multiplexer_2_out, multiplexer_3_out;

  Multiplexer #(.width(4)) multiplexer_1 (
    .in0(Chute_do_jogador_A), .in1(4'b0000), .out(multiplexer_1_out), .sel(A_DEAD));  // open: en
  Multiplexer #(.width(4)) multiplexer_2 (
    .in0(Chute_do_jogador_B), .in1(4'b0000), .out(multiplexer_2_out), .sel(B_DEAD));  // open: en
  Multiplexer #(.width(4)) multiplexer_3 (
    .in0(multiplexer_1_out), .in1(multiplexer_2_out), .out(multiplexer_3_out), .sel(Turno__0___A__1___B));  // open: en
  Register #(.width(4)) Registra_X (
    .D(multiplexer_3_out), .Q(X_chutado_no_momento), .clk(and_1_out), .clr(Reset));  // open: en
  and and_1 (and_1_out, Chutar, Coordenada__0___X__1___Y_qn);
  Register #(.width(4)) Registra_Y (
    .D(multiplexer_3_out), .Q(Y_chutado_no_momento), .clk(and_2_out), .clr(Reset));  // open: en
  and and_2 (and_2_out, Chutar, Coordenada__0___X__1___Y_q);
  T_Flip_Flop Coordenada__0___X__1___Y (
    .clk(\Próximo ), .T(\Próximo ), .Q(Coordenada__0___X__1___Y_q), .Qn(Coordenada__0___X__1___Y_qn),
    .reset(Reset));  // open: preset, en
  and and_3 (Maior, Exibindo_resultado_do_chute, comparador_de_palpites_1_maior);
  not not_1 (not_1_out, Coordenada__0___X__1___Y_q);
  Comparador_de_palpites comparador_de_palpites_1 (
    .\Gerar_X_e_Y_aleatórios (\Gerar_aleatório ), .Palpite_X(X_chutado_no_momento),
    .Palpite_Y(Y_chutado_no_momento), .Acertou(comparador_de_palpites_1_acertou),
    .Menor(comparador_de_palpites_1_menor), .Igual(comparador_de_palpites_1_igual),
    .Maior(comparador_de_palpites_1_maior));  // open: Valor_correto_de_Y, Valor_correto_de_X
  and and_4 (Igual, Exibindo_resultado_do_chute, comparador_de_palpites_1_igual);
  and and_5 (Aguardando_chute_Y, Coordenada__0___X__1___Y_q, ~Exibindo_resultado_do_chute);  // AND_Gate
  and and_6 (Aguardando_chute_X, Coordenada__0___X__1___Y_qn, ~Exibindo_resultado_do_chute);  // AND_Gate
  T_Flip_Flop Exibindo (
    .clk(not_1_out), .T(1'b1), .Q(Exibindo_resultado_do_chute), .reset(Reset));  // open: Qn, preset, en
  and and_7 (Menor, Exibindo_resultado_do_chute, comparador_de_palpites_1_menor);
  not not_2 (not_2_out, Exibindo_resultado_do_chute);
  and and_8 (Acertou, Exibindo_resultado_do_chute, comparador_de_palpites_1_acertou);
  T_Flip_Flop Turno (.clk(not_2_out), .T(1'b1), .Q(Turno__0___A__1___B), .reset(Reset));  // open: Qn, preset, en

  // Other names for the same wires on the sheet: e = Exibindo_resultado_do_chute; r = Reset

  // Notes on the sheet:
  //   Registra A se CHUTAR e COORDENADA = A
  //   Exibe quando Y vai de 1 para 0
  //   Aguarda chute A se COORDENADA = A e não estiver exibindo
  //   Troca turno quando exibição vai de 1 para 0
endmodule

module \Cronômetro  (
  input  Clock,
  input  Clear,
  input  Altera_dezena_de_minuto,
  input  Altera_unidade_de_minuto,
  input  Altera_dezena_de_segundo,
  input  Altera_unidade_de_segundo,
  input  Pause,
  input  Config,
  output End,
  output [3:0] Dezena_de_minuto,
  output [3:0] Unidade_de_minuto,
  output [3:0] Dezena_de_segundo,
  output [3:0] Unidade_de_segundo
);

  wire and_2_out, and_3_out, and_4_out, and_5_out, \dezena_1_sinal_p__próximo , \dezena_2_sinal_p__próximo ,
       or_1_out, \unidade_1_sinal_p__próximo , \unidade_2_sinal_p__próximo ;

  and and_1 (End, and_2_out, and_3_out, and_4_out, and_5_out);
  and and_2 (and_2_out, ~Dezena_de_minuto[3], ~Dezena_de_minuto[2], ~Dezena_de_minuto[1], ~Dezena_de_minuto[0]);  // AND_Gate
  Dezena dezena_1 (
    .Clk(\unidade_1_sinal_p__próximo ), .Alterar(Altera_dezena_de_minuto),
    .\Sinal_p__próximo (\dezena_1_sinal_p__próximo ), .Clear(Clear), .Valor(Dezena_de_minuto),
    .Mode(or_1_out), .Pause(Pause));
  and and_3 (and_3_out, ~Unidade_de_minuto[3], ~Unidade_de_minuto[2], ~Unidade_de_minuto[1], ~Unidade_de_minuto[0]);  // AND_Gate
  Unidade unidade_1 (
    .\Sinal_p__próximo (\unidade_1_sinal_p__próximo ), .Mode(or_1_out), .Valor(Unidade_de_minuto),
    .Pause(Pause), .Clk(\dezena_2_sinal_p__próximo ), .Clear(Clear), .Alterar(Altera_unidade_de_minuto));
  and and_4 (and_4_out, ~Dezena_de_segundo[3], ~Dezena_de_segundo[2], ~Dezena_de_segundo[1], ~Dezena_de_segundo[0]);  // AND_Gate
  Dezena dezena_2 (
    .Clk(\unidade_2_sinal_p__próximo ), .Alterar(Altera_dezena_de_segundo),
    .\Sinal_p__próximo (\dezena_2_sinal_p__próximo ), .Clear(Clear), .Valor(Dezena_de_segundo),
    .Mode(or_1_out), .Pause(Pause));
  and and_5 (and_5_out, ~Unidade_de_segundo[3], ~Unidade_de_segundo[2], ~Unidade_de_segundo[1], ~Unidade_de_segundo[0]);  // AND_Gate
  Unidade unidade_2 (
    .\Sinal_p__próximo (\unidade_2_sinal_p__próximo ), .Mode(or_1_out), .Valor(Unidade_de_segundo),
    .Pause(Pause), .Clk(Clock), .Clear(Clear), .Alterar(Altera_unidade_de_segundo));
  or or_1 (or_1_out, End, Config);
endmodule

module Placar (
  input  A_pontuou,
  input  B_pontuou,
  input  Reset,
  output [3:0] Placar_A,
  output [3:0] Placar_B,
  output Fim_de_jogo,
  output A_venceu,
  output B_venceu,
  output Empate
);

  wire and_1_out, and_2_out;
  wire [3:0] adder_1_out, adder_2_out;

  Adder #(.width(4)) adder_1 (.a(Placar_A), .b(4'b0001), .out(adder_1_out));  // open: cin, cout
  Adder #(.width(4)) adder_2 (.a(Placar_B), .b(4'b0001), .out(adder_2_out));  // open: cin, cout
  Register #(.width(4)) register_1 (.D(adder_1_out), .Q(Placar_A), .clk(A_pontuou), .clr(Reset));  // open: en
  Register #(.width(4)) register_2 (.D(adder_2_out), .Q(Placar_B), .clk(B_pontuou), .clr(Reset));  // open: en
  and and_1 (and_1_out, Placar_A[0], Placar_A[1], Placar_A[2], Placar_A[3]);
  and and_2 (and_2_out, Placar_B[0], Placar_B[1], Placar_B[2], Placar_B[3]);
  and and_3 (A_venceu, and_1_out, ~and_2_out);  // AND_Gate
  and and_4 (B_venceu, ~and_1_out, and_2_out);  // AND_Gate
  and and_5 (Empate, and_1_out, and_2_out);
  or or_1 (Fim_de_jogo, A_venceu, B_venceu, Empate);

  // Other names for the same wires on the sheet: r = Reset
endmodule

module Comparador_de_palpites (
  input  \Gerar_X_e_Y_aleatórios ,
  input  [3:0] Palpite_X,
  input  [3:0] Palpite_Y,
  output Acertou,
  output [3:0] Valor_correto_de_X,
  output Menor,
  output [3:0] Valor_correto_de_Y,
  output Igual,
  output Maior
);

  wire comparator_1_eq;
  wire [3:0] adder_1_out, adder_2_out;

  Random #(.width(4)) random_1 (.clk(\Gerar_X_e_Y_aleatórios ), .out(Valor_correto_de_X));  // open: next, clr
  Random #(.width(4)) random_2 (.clk(\Gerar_X_e_Y_aleatórios ), .out(Valor_correto_de_Y));  // open: next, clr
  Adder #(.width(4)) adder_1 (.a(Palpite_X), .b(Palpite_Y), .out(adder_1_out));  // open: cin, cout
  Adder #(.width(4)) adder_2 (.a(Valor_correto_de_X), .b(Valor_correto_de_Y), .out(adder_2_out));  // open: cin, cout
  Comparator #(.width(4)) comparator_1 (.a(Valor_correto_de_X), .b(Palpite_X), .eq(comparator_1_eq));  // open: gt, lt
  Comparator #(.width(4)) comparator_2 (.a(adder_2_out), .b(adder_1_out), .gt(Menor), .eq(Igual), .lt(Maior));
  and and_1 (Acertou, comparator_1_eq, Igual);
endmodule

module Unidade (
  input  Clear,
  input  Clk,
  input  Alterar,
  input  Mode,
  input  Pause,
  output [3:0] Valor,
  output \Sinal_p__próximo 
);

  wire multiplexer_1_out, multiplexer_2_out, or_1_out, or_2_out;
  wire [3:0] subtractor_1_out;

  Subtractor #(.width(4)) subtractor_1 (.a(Valor), .b(4'b0001), .out(subtractor_1_out));  // open: bin, bout
  Multiplexer multiplexer_1 (.in0(Clk), .in1(Alterar), .out(multiplexer_1_out), .sel(Mode));  // open: en
  Multiplexer multiplexer_2 (.in0(multiplexer_1_out), .in1(1'b0), .out(multiplexer_2_out), .sel(Pause));  // open: en
  D_Flip_Flop d_ff_1 (
    .clk(multiplexer_2_out), .D(subtractor_1_out[3]), .Q(Valor[3]), .preset(\Sinal_p__próximo ), .reset(Clear));  // open: Qn, en
  D_Flip_Flop d_ff_2 (
    .clk(multiplexer_2_out), .D(subtractor_1_out[2]), .Q(Valor[2]), .reset(or_1_out));  // open: Qn, preset, en
  D_Flip_Flop d_ff_3 (
    .clk(multiplexer_2_out), .D(subtractor_1_out[1]), .Q(Valor[1]), .reset(or_2_out));  // open: Qn, preset, en
  D_Flip_Flop d_ff_4 (
    .clk(multiplexer_2_out), .D(subtractor_1_out[0]), .Q(Valor[0]), .preset(\Sinal_p__próximo ), .reset(Clear));  // open: Qn, en
  or or_1 (or_1_out, \Sinal_p__próximo , Clear);
  or or_2 (or_2_out, \Sinal_p__próximo , Clear);
  and and_1 (\Sinal_p__próximo , Valor[3], Valor[2], Valor[1], Valor[0]);
endmodule

module Dezena (
  input  Clear,
  input  Clk,
  input  Alterar,
  input  Mode,
  input  Pause,
  output [3:0] Valor,
  output \Sinal_p__próximo 
);

  wire multiplexer_1_out, multiplexer_2_out, or_1_out, or_2_out;
  wire [3:0] subtractor_1_out;

  Subtractor #(.width(4)) subtractor_1 (.a(Valor), .b(4'b0001), .out(subtractor_1_out));  // open: bin, bout
  Multiplexer multiplexer_1 (.in0(Clk), .in1(Alterar), .out(multiplexer_1_out), .sel(Mode));  // open: en
  Multiplexer multiplexer_2 (.in0(multiplexer_1_out), .in1(1'b0), .out(multiplexer_2_out), .sel(Pause));  // open: en
  D_Flip_Flop d_ff_1 (
    .clk(multiplexer_2_out), .D(subtractor_1_out[3]), .Q(Valor[3]), .reset(or_1_out));  // open: Qn, preset, en
  D_Flip_Flop d_ff_2 (
    .clk(multiplexer_2_out), .D(subtractor_1_out[2]), .Q(Valor[2]), .preset(\Sinal_p__próximo ), .reset(Clear));  // open: Qn, en
  D_Flip_Flop d_ff_3 (
    .clk(multiplexer_2_out), .D(subtractor_1_out[1]), .Q(Valor[1]), .reset(or_2_out));  // open: Qn, preset, en
  D_Flip_Flop d_ff_4 (
    .clk(multiplexer_2_out), .D(subtractor_1_out[0]), .Q(Valor[0]), .preset(\Sinal_p__próximo ), .reset(Clear));  // open: Qn, en
  or or_1 (or_1_out, Clear, \Sinal_p__próximo );
  or or_2 (or_2_out, Clear, \Sinal_p__próximo );
  and and_1 (\Sinal_p__próximo , Valor[3], Valor[2], Valor[1], Valor[0]);
endmodule

module Mostra_sinal_negativo (
);

  wire and_1_out, and_2_out, or_1_out, undriven, undriven_2, undriven_3, undriven_4;

  or or_1 (or_1_out, and_1_out, and_2_out);
  and and_1 (and_1_out, ~undriven, undriven_2);  // AND_Gate
  and and_2 (and_2_out, undriven_3, undriven_4);
endmodule

module Registrador (
  input  Clk,
  input  B1,
  input  B2,
  input  B3,
  input  B4,
  output S1,
  output S2,
  output S3,
  output S4
);

  D_Flip_Flop d_ff_1 (.clk(Clk), .D(B1), .Q(S1));  // open: Qn, preset, en, reset
  D_Flip_Flop d_ff_2 (.clk(Clk), .D(B2), .Q(S2));  // open: Qn, preset, en, reset
  D_Flip_Flop d_ff_3 (.clk(Clk), .D(B3), .Q(S3));  // open: Qn, preset, en, reset
  D_Flip_Flop d_ff_4 (.clk(Clk), .D(B4), .Q(S4));  // open: Qn, preset, en, reset
endmodule

module ValoresPlano (
  input  [3:0] Valores_de_entrada,
  output [3:0] Valores_de_saida,
  output Sinal_negativo
);

  wire [3:0] adder_1_out, not_3_out;

  not not_1 (not_3_out[3], Valores_de_entrada[3]);
  not not_2 (not_3_out[2], Valores_de_entrada[2]);
  not not_3 (not_3_out[0], Valores_de_entrada[0]);
  not not_4 (not_3_out[1], Valores_de_entrada[1]);
  Adder #(.width(4)) adder_1 (.a(not_3_out), .b(4'b0001), .out(adder_1_out));  // open: cin, cout
  Multiplexer #(.width(4)) multiplexer_1 (
    .in0(Valores_de_entrada), .in1(adder_1_out), .out(Valores_de_saida), .sel(Valores_de_entrada[3]));  // open: en

  assign Sinal_negativo = Valores_de_entrada[3];
endmodule

module Teste_1 (
  input  Chutar,
  input  Proximo,
  input  B3,
  input  B2,
  input  B1,
  input  B0,
  input  B3_2,
  input  B2_2,
  input  B1_2,
  input  B0_2,
  output Errou,
  output Acertou,
  output Menor,
  output Igual,
  output Maior
);

  wire and_1_out, and_2_out, and_3_out, and_4_out, button_2_out, button_3_out, comparador_de_palpites_1_p1,
       d_ff_1_q, d_ff_2_q, d_ff_3_q, d_ff_4_q, not_1_out, not_2_out, not_3_out, or_1_out, or_2_out,
       valoresplano_1_sinal_negativo, valoresplano_2_sinal_negativo;
  wire [3:0] comparador_de_palpites_1_p7, register_1_q, register_2_q, valoresplano_1_valores_de_saida,
       valoresplano_2_valores_de_saida;

  LED led_1 (.in(valoresplano_1_sinal_negativo));
  Hex_Digit_Display hex_digit_display_1 (.value(valoresplano_1_valores_de_saida));  // open: dp
  ValoresPlano valoresplano_1 (
    .Valores_de_entrada({B3, B2, B1, B0}), .Valores_de_saida(valoresplano_1_valores_de_saida),
    .Sinal_negativo(valoresplano_1_sinal_negativo));
  LED led_2 (.in(or_1_out));
  or or_1 (or_1_out, and_1_out, and_2_out);
  and and_1 (and_1_out, ~button_3_out, d_ff_1_q);  // AND_Gate
  and and_2 (and_2_out, button_3_out, d_ff_3_q);
  // Comparador_de_palpites comparador_de_palpites_1: pin names not known; wires that end beside it: comparador_de_palpites_1_p1, Errou, Acertou, Menor, Igual, Maior, comparador_de_palpites_1_p7, comparador_de_palpites_1_p7
  Button button_1 (.out(comparador_de_palpites_1_p1));
  Hex_Digit_Display hex_digit_display_2 (.value(register_1_q));  // open: dp
  Register #(.width(4)) register_1 (
    .D(comparador_de_palpites_1_p7), .Q(register_1_q), .clk(button_2_out));  // open: en, clr
  Button button_2 (.out(button_2_out));
  Multiplexer #(.width(4)) multiplexer_1 (
    .in0(valoresplano_1_valores_de_saida), .in1(valoresplano_2_valores_de_saida),
    .out(comparador_de_palpites_1_p7), .sel(button_3_out));  // open: en
  not not_1 (not_1_out, button_2_out);
  D_Flip_Flop d_ff_1 (
    .clk(button_2_out), .D(valoresplano_1_sinal_negativo), .Q(d_ff_1_q));  // open: Qn, preset, en, reset
  not not_2 (not_2_out, button_2_out);
  Button button_3 (.out(button_3_out));
  D_Flip_Flop d_ff_2 (.clk(not_1_out), .D(valoresplano_1_sinal_negativo), .Q(d_ff_2_q));  // open: Qn, preset, en, reset
  LED led_3 (.in(or_2_out));
  Register #(.width(4)) register_2 (
    .D(comparador_de_palpites_1_p7), .Q(register_2_q), .clk(not_2_out));  // open: en, clr
  D_Flip_Flop d_ff_3 (
    .clk(button_2_out), .D(valoresplano_2_sinal_negativo), .Q(d_ff_3_q));  // open: Qn, preset, en, reset
  not not_3 (not_3_out, button_2_out);
  Hex_Digit_Display hex_digit_display_3 (.value(register_2_q));  // open: dp
  D_Flip_Flop d_ff_4 (.clk(not_3_out), .D(valoresplano_2_sinal_negativo), .Q(d_ff_4_q));  // open: Qn, preset, en, reset
  or or_2 (or_2_out, and_3_out, and_4_out);
  and and_3 (and_3_out, ~button_3_out, d_ff_2_q);  // AND_Gate
  and and_4 (and_4_out, button_3_out, d_ff_4_q);
  LED led_4 (.in(valoresplano_2_sinal_negativo));
  Hex_Digit_Display hex_digit_display_4 (.value(valoresplano_2_valores_de_saida));  // open: dp
  ValoresPlano valoresplano_2 (
    .Valores_de_entrada({B3_2, B2_2, B1_2, B0_2}), .Valores_de_saida(valoresplano_2_valores_de_saida),
    .Sinal_negativo(valoresplano_2_sinal_negativo));
endmodule

module \Teste_do_cronômetro  (
  input  Pause,
  input  Config
);

  wire Clear_out, clock_1_out, \cronômetro_1_end , DM_out, DS_out, UM_out, US_out;
  wire [3:0] \cronômetro_1_dezena_de_minuto , \cronômetro_1_dezena_de_segundo ,
       \cronômetro_1_unidade_de_minuto , \cronômetro_1_unidade_de_segundo ;

  LED End (.in(\cronômetro_1_end ));
  Button DM (.out(DM_out));
  Hex_Digit_Display hex_digit_display_1 (.value(\cronômetro_1_unidade_de_minuto ));  // open: dp
  Hex_Digit_Display hex_digit_display_2 (.value(\cronômetro_1_dezena_de_minuto ));  // open: dp
  Button DS (.out(DS_out));
  Button UM (.out(UM_out));
  Hex_Digit_Display hex_digit_display_3 (.value(\cronômetro_1_dezena_de_segundo ));  // open: dp
  Button US (.out(US_out));
  Hex_Digit_Display hex_digit_display_4 (.value(\cronômetro_1_unidade_de_segundo ));  // open: dp
  \Cronômetro  \cronômetro_1  (
    .End(\cronômetro_1_end ), .Dezena_de_minuto(\cronômetro_1_dezena_de_minuto ),
    .Unidade_de_minuto(\cronômetro_1_unidade_de_minuto ),
    .Dezena_de_segundo(\cronômetro_1_dezena_de_segundo ),
    .Unidade_de_segundo(\cronômetro_1_unidade_de_segundo ), .Clock(clock_1_out), .Pause(Pause),
    .Config(Config), .Clear(Clear_out), .Altera_dezena_de_minuto(DM_out), .Altera_unidade_de_minuto(UM_out),
    .Altera_dezena_de_segundo(DS_out), .Altera_unidade_de_segundo(US_out));
  Button Clear (.out(Clear_out));
  Clock clock_1 (.out(clock_1_out));
endmodule

module reserva (
  input  A0,
  input  A1,
  input  A2,
  input  A3
);

  wire decodificador_1_a_2, decodificador_1_b_2, decodificador_1_c_2, decodificador_1_d_2, decodificador_1_e,
       decodificador_1_f, decodificador_1_g;

  _7_Segment_Display u_7_segment_display_1 (
    .g(decodificador_1_g), .f(decodificador_1_f), .a(decodificador_1_a_2), .b(decodificador_1_b_2),
    .e(decodificador_1_e), .d(decodificador_1_d_2), .c(decodificador_1_c_2));  // open: dp
  decodificador decodificador_1 (
    .a(A0), .b(A1), .c(A2), .d(A3), .a_2(decodificador_1_a_2), .b_2(decodificador_1_b_2),
    .c_2(decodificador_1_c_2), .d_2(decodificador_1_d_2), .e(decodificador_1_e), .f(decodificador_1_f),
    .g(decodificador_1_g));
endmodule

module decodificador (
  input  a,
  input  b,
  input  c,
  input  d,
  output a_2,
  output b_2,
  output c_2,
  output d_2,
  output e,
  output f,
  output g
);

  wire and_1_out, and_2_out, and_3_out, and_4_out, and_5_out, and_6_out, and_7_out, and_8_out, and_9_out,
       and_10_out, and_11_out, and_12_out, and_13_out, and_14_out, and_15_out, and_16_out, and_17_out,
       and_18_out, and_19_out, and_20_out, and_21_out, and_22_out, and_23_out, and_24_out, and_25_out,
       and_26_out, and_27_out, and_28_out, and_29_out, and_30_out, and_31_out, and_32_out, and_33_out,
       and_34_out;

  and and_1 (and_1_out, ~b, ~d);  // AND_Gate
  and and_2 (and_2_out, ~a, c);  // AND_Gate
  and and_3 (and_3_out, ~a, b, d);  // AND_Gate
  and and_4 (and_4_out, b, c);
  and and_5 (and_5_out, a, ~b, ~c);  // AND_Gate
  and and_6 (and_6_out, a, ~d);  // AND_Gate
  and and_7 (and_7_out, ~a, ~c, ~d);  // AND_Gate
  and and_8 (and_8_out, ~b, ~d);  // AND_Gate
  and and_9 (and_9_out, ~a, c, d);  // AND_Gate
  and and_10 (and_10_out, a, ~c, d);  // AND_Gate
  and and_11 (and_11_out, ~a, ~c, ~d);  // AND_Gate
  and and_12 (and_12_out, ~a, c, d);  // AND_Gate
  and and_13 (and_13_out, ~a, b);  // AND_Gate
  and and_14 (and_14_out, a, ~b);  // AND_Gate
  and and_15 (and_15_out, a, ~c, d);  // AND_Gate
  and and_16 (and_16_out, ~a, ~b, ~d);  // AND_Gate
  and and_17 (and_17_out, ~b, c, d);  // AND_Gate
  and and_18 (and_18_out, b, ~c, d);  // AND_Gate
  and and_19 (and_19_out, b, c, ~d);  // AND_Gate
  and and_20 (and_20_out, a, ~c);  // AND_Gate
  and and_21 (and_21_out, ~a, ~b, ~c);  // AND_Gate
  and and_22 (and_22_out, ~b, ~d);  // AND_Gate
  and and_23 (and_23_out, c, ~d);  // AND_Gate
  and and_24 (and_24_out, a, c);
  and and_25 (and_25_out, a, b);
  and and_26 (and_26_out, ~a, ~c);  // AND_Gate
  and and_27 (and_27_out, ~c, ~d);  // AND_Gate
  and and_28 (and_28_out, b, c);
  and and_29 (and_29_out, a, ~b);  // AND_Gate
  and and_30 (and_30_out, ~b, c);  // AND_Gate
  and and_31 (and_31_out, c, ~d);  // AND_Gate
  and and_32 (and_32_out, ~a, b, ~c);  // AND_Gate
  and and_33 (and_33_out, a, ~b);  // AND_Gate
  and and_34 (and_34_out, a, d);
  or or_1 (a_2, and_1_out, and_2_out, and_3_out, and_4_out, and_5_out, and_6_out);
  or or_2 (b_2, and_7_out, and_8_out, and_9_out, and_10_out);
  or or_3 (c_2, and_11_out, and_12_out, and_13_out, and_14_out, and_15_out);
  or or_4 (d_2, and_16_out, and_17_out, and_18_out, and_19_out, and_20_out);
  or or_5 (e, and_21_out, and_22_out, and_23_out, and_24_out, and_25_out);
  or or_6 (f, and_26_out, and_27_out, and_28_out, and_29_out);
  or or_7 (g, and_30_out, and_31_out, and_32_out, and_33_out, and_34_out);
endmodule
